# Fritzing sketch Matrix 8x8 Game Breadboards (saved by Fritzing 0.9.3b)
perfboards: 2

parts:
  J1 = Piezo Speaker
  RCWL-0516_Microwave_Radar_Motion_Sensor1 = RCWL-0516 Microwave Radar Motion Sensor Module  # not connected
  Nano1 = Arduino Nano v2.3  # not connected
  R10 = Resistor [tolerance=±5% resistance=1k package="2512 [SMD]"]  # not connected
  JP1 = Header 8 [package=1x08_smd]  # not connected
  JP2 = Header 8 [package=1x08_smd]  # not connected
  JP3 = Header 8 [package=1x08_smd]  # not connected
  JP4 = Header 8 [package=1x08_smd]  # not connected
  JP5 = Header 8 [package=1x08_smd]  # not connected
  JP6 = Header 8 [package=1x08_smd]  # not connected
  R12 = Resistor [tolerance=±5% resistance=1k package="2512 [SMD]"]  # not connected
  R13 = Resistor [tolerance=±5% resistance=1k package="2512 [SMD]"]  # not connected
  R14 = Resistor [tolerance=±5% resistance=1k package="2512 [SMD]"]  # not connected
  R15 = Resistor [tolerance=±5% resistance=1k package="2512 [SMD]"]  # not connected
  R17 = Resistor [tolerance=±5% resistance=1k package="2512 [SMD]"]  # not connected
  R18 = Resistor [tolerance=±5% resistance=1k package="2512 [SMD]"]  # not connected
  R19 = Resistor [tolerance=±5% resistance=1k package="2512 [SMD]"]  # not connected
  R20 = Resistor [tolerance=±5% resistance=1M package="2512 [SMD]"]
  J2 = Piezo Speaker

nets:
  N1: J1.pin1, R20.Pin_0, J2.pin1
  N2: J1.pin2, R20.Pin_1

custom parts:
  RCWL-0516 Microwave Radar Motion Sensor Module: The RCWL-0516 is a microwave radar motion sensor module. Input voltage is 4V to 28V. The 3V3 pin is a power output.
